// Logisim project crc.circ as structural Verilog: 2 circuits, main circuit CRC
module CRC (
  input  [7:0] \input ,
  input  [3:0] divisor,
  output [10:0] out_3
);

  wire [2:0] mod4_1_remaider, mod4_2_remaider, mod4_3_remaider, mod4_4_remaider, mod4_5_remaider,
       mod4_6_remaider, mod4_7_remaider;

  mod4 mod4_1 (.supply(\input [4]), .remaining(\input [7:5]), .divisor(divisor), .remaider(mod4_1_remaider));
  mod4 mod4_2 (.supply(\input [3]), .remaining(mod4_1_remaider), .divisor(divisor), .remaider(mod4_2_remaider));
  mod4 mod4_3 (.supply(\input [2]), .remaining(mod4_2_remaider), .divisor(divisor), .remaider(mod4_3_remaider));
  mod4 mod4_4 (.supply(\input [1]), .remaining(mod4_3_remaider), .divisor(divisor), .remaider(mod4_4_remaider));
  mod4 mod4_5 (.supply(\input [0]), .remaining(mod4_4_remaider), .divisor(divisor), .remaider(mod4_5_remaider));
  mod4 mod4_6 (.supply(1'b0), .remaining(mod4_5_remaider), .divisor(divisor), .remaider(mod4_6_remaider));
  mod4 mod4_7 (.supply(1'b0), .remaining(mod4_6_remaider), .divisor(divisor), .remaider(mod4_7_remaider));
  mod4 mod4_8 (.supply(1'b0), .remaining(mod4_7_remaider), .divisor(divisor), .remaider(out_3[2:0]));

  assign out_3[10:3] = \input ;
endmodule

module mod4 (
  input  supply,
  input  [2:0] remaining,
  input  [3:0] divisor,
  output [2:0] remaider
);

  wire [3:0] xor_1_out;

  assign xor_1_out = {remaining, supply} ^ divisor;  // XOR_Gate xor_1, 4 bits wide
  Multiplexer #(.width(3)) multiplexer_1 (
    .in0(xor_1_out[2:0]), .in1({remaining[1:0], supply}), .out(remaider), .sel(xor_1_out[3]));  // open: en
endmodule
