// Logisim project fsm.circ as structural Verilog: 2 circuits, main circuit fsm
module fsm (
  input  clear,
  input  [1:0] \input ,
  output Z
);

  wire clk, comparator_1_eq, comparator_2_eq, comparator_3_eq, or_1_out;
  wire [1:0] detection_1_now_state, multiplexer_1_out, state_q;

  Clock clock_1 (.out(clk));
  detection detection_1 (.\input (\input ), .pre_state(state_q), .now_state(detection_1_now_state));
  Comparator #(.width(2)) comparator_1 (.a(2'b00), .b(\input ), .eq(comparator_1_eq));  // open: gt, lt
  Comparator #(.width(2)) comparator_2 (.a(\input ), .b(2'b10), .eq(comparator_2_eq));  // open: gt, lt
  Multiplexer #(.width(2)) multiplexer_1 (
    .in0(detection_1_now_state), .in1(2'b00), .out(multiplexer_1_out), .sel(clear));  // open: en
  Register #(.width(2)) state (.D(multiplexer_1_out), .Q(state_q), .clk(clk));  // open: en, clr
  or or_1 (or_1_out, comparator_1_eq, comparator_2_eq);
  Comparator #(.width(2)) comparator_3 (.a(2'b10), .b(state_q), .eq(comparator_3_eq));  // open: gt, lt
  and and_1 (Z, or_1_out, comparator_3_eq);

  // Other names for the same wires on the sheet: reset = clear
endmodule

module detection (
  input  [1:0] \input ,
  input  [1:0] pre_state,
  output [1:0] now_state
);

  wire [1:0] _00, _01, _10, _11, demultiplexer_1_out0, demultiplexer_1_out1, demultiplexer_1_out2,
       demultiplexer_1_out3;

  Demultiplexer #(.select(2), .width(2)) demultiplexer_1 (
    .out0(demultiplexer_1_out0), .out1(demultiplexer_1_out1), .out2(demultiplexer_1_out2),
    .out3(demultiplexer_1_out3), .in(\input ), .sel(pre_state));  // open: en
  Multiplexer #(.select(2), .width(2)) multiplexer_1 (
    .in0(2'b00), .in1(2'b01), .in2(2'b00), .in3(2'b00), .out(_00), .sel(demultiplexer_1_out0));  // open: en
  Multiplexer #(.select(2), .width(2)) multiplexer_2 (
    .in0(2'b10), .in1(2'b01), .in2(2'b10), .in3(2'b00), .out(_01), .sel(demultiplexer_1_out1));  // open: en
  Multiplexer #(.select(2), .width(2)) multiplexer_3 (
    .in0(2'b00), .in1(2'b01), .in2(2'b00), .in3(2'b00), .out(_11), .sel(demultiplexer_1_out3));  // open: en
  Multiplexer #(.select(2), .width(2)) multiplexer_4 (
    .in0(2'b11), .in1(2'b00), .in2(2'b11), .in3(2'b00), .out(_10), .sel(demultiplexer_1_out2));  // open: en
  Multiplexer #(.select(2), .width(2)) multiplexer_5 (
    .in0(_00), .in1(_01), .in2(_10), .in3(_11), .out(now_state), .sel(pre_state));  // open: en
endmodule
