// Logisim project ftoi.circ as structural Verilog: 1 circuit, main circuit ftoi
module ftoi (
  input  [15:0] in_1,
  output [31:0] out_2
);

  wire and_1_out, comparator_1_lt, comparator_2_gt, comparator_3_lt;
  wire [4:0] adder_1_out, negator_1_out, subtractor_1_out;
  wire [15:0] shifter_1_out;
  wire [31:0] multiplexer_1_out, multiplexer_2_out, negator_2_out;

  Subtractor #(.width(5)) subtractor_1 (.a(in_1[14:10]), .b(5'b01111), .out(subtractor_1_out));  // open: bin, bout
  // Probe on negator_1_out
  Negator #(.width(5)) negator_1 (.in(adder_1_out), .out(negator_1_out));
  Adder #(.width(5)) adder_1 (.a(5'b00001), .b(subtractor_1_out), .out(adder_1_out));  // open: cin, cout
  Comparator #(.width(5), .mode("unsigned")) comparator_1 (
    .a(in_1[14:10]), .b({5{1'b1}}), .lt(comparator_1_lt));  // open: gt, eq
  Comparator #(.width(5), .mode("unsigned")) comparator_2 (
    .a(in_1[14:10]), .b({5{1'b0}}), .gt(comparator_2_gt));  // open: eq, lt
  Shifter #(.width(16), .shift("lr")) shifter_1 (
    .in({1'b1, in_1[9:0], {5{1'b0}}}), .\dist (negator_1_out[3:0]), .out(shifter_1_out));
  Comparator #(.width(5)) comparator_3 (.a(subtractor_1_out), .b({5{1'b0}}), .lt(comparator_3_lt));  // open: gt, eq
  and and_1 (and_1_out, comparator_1_lt, comparator_2_gt);
  Multiplexer #(.width(32)) multiplexer_1 (
    .in0({{16{1'b0}}, shifter_1_out}), .in1({32{1'b0}}), .out(multiplexer_1_out), .sel(comparator_3_lt));  // open: en
  Multiplexer #(.width(32)) multiplexer_2 (
    .in0(multiplexer_1_out), .in1(negator_2_out), .out(multiplexer_2_out), .sel(in_1[15]));  // open: en
  Negator #(.width(32)) negator_2 (.in(multiplexer_1_out), .out(negator_2_out));
  Multiplexer #(.width(32)) multiplexer_3 (
    .in0({32{1'b0}}), .in1(multiplexer_2_out), .out(out_2), .sel(and_1_out));  // open: en

  // Other names for the same wires on the sheet: sign = in_1[15]
endmodule
