// Logisim project navigation.circ as structural Verilog: 2 circuits, main circuit navigation
module navigation (
  input  [1:0] direction,
  input  clk,
  input  reset,
  output arrive,
  output hit
);

  wire move_1_hit;
  wire [2:0] move_1_now_state, state_q;

  move move_1 (.dir(direction), .pre_state(state_q), .now_state(move_1_now_state), .hit(move_1_hit));
  Register #(.width(1)) u_hit (.D(move_1_hit), .Q(hit), .clk(clk), .clr(reset));  // open: en
  Register #(.width(3)) state (.D(move_1_now_state), .Q(state_q), .clk(clk), .clr(reset));  // open: en
  Comparator #(.width(3)) comparator_1 (.a(3'b100), .b(state_q), .eq(arrive));  // open: gt, lt
endmodule

module move (
  input  [1:0] dir,
  input  [2:0] pre_state,
  output [2:0] now_state,
  output hit
);

  wire [1:0] demultiplexer_1_out0, demultiplexer_1_out1, demultiplexer_1_out2, demultiplexer_1_out3,
       demultiplexer_1_out4;
  wire [2:0] _000_A, _001_C, _010_D, _011_E, _100_B;

  Demultiplexer #(.select(3), .width(2), .tristate("true")) demultiplexer_1 (
    .out0(demultiplexer_1_out0), .out1(demultiplexer_1_out1), .out2(demultiplexer_1_out2),
    .out3(demultiplexer_1_out3), .out4(demultiplexer_1_out4), .in(dir), .sel(pre_state));  // open: out5, out6, out7, en
  Multiplexer #(.select(2), .width(3)) multiplexer_1 (
    .in0(3'b001), .in1(3'b000), .in2(3'b000), .in3(3'b000), .out(_000_A), .sel(demultiplexer_1_out0));  // open: en
  Multiplexer #(.select(2), .width(3)) multiplexer_2 (
    .in0(3'b011), .in1(3'b010), .in2(3'b000), .in3(3'b001), .out(_001_C), .sel(demultiplexer_1_out1));  // open: en
  Multiplexer #(.select(2), .width(3)) multiplexer_3 (
    .in0(3'b100), .in1(3'b010), .in2(3'b010), .in3(3'b001), .out(_010_D), .sel(demultiplexer_1_out2));  // open: en
  Multiplexer #(.select(3), .width(3)) multiplexer_4 (
    .in0(_000_A), .in1(_001_C), .in2(_010_D), .in3(_011_E), .in4(_100_B), .out(now_state), .sel(pre_state));  // open: in5, in6, in7, en
  Multiplexer #(.select(2), .width(3)) multiplexer_5 (
    .in0(3'b011), .in1(3'b100), .in2(3'b001), .in3(3'b011), .out(_011_E), .sel(demultiplexer_1_out3));  // open: en
  Comparator #(.width(3)) comparator_1 (.a(now_state), .b(pre_state), .eq(hit));  // open: gt, lt
  Multiplexer #(.select(2), .width(3)) multiplexer_6 (
    .in0(3'b000), .in1(3'b000), .in2(3'b000), .in3(3'b000), .out(_100_B), .sel(demultiplexer_1_out4));  // open: en
endmodule
